# Fritzing sketch Sketch Motors (saved by Fritzing 0.9.3b)
breadboards: 1

parts:
  IC1 = L293D [package=THT]
  VCC1 = 4 x AAA Battery Mount
  M1 = DC Motor
  M2 = DC Motor
  Composant1 = Arduino Uno (Rev3)
  hc-sr1 = hc-sr04

nets:
  N1: IC1.Enable_1, Composant1.D2
  N2: IC1.In_1, Composant1.D3_PWM
  N3: IC1.Out_1_(_Controlled_by_Enable_1_), M2.pin_1
  GND: IC1.0V, VCC1.-, Composant1.GND, hc-sr1.GND
  N4: IC1.Out_2_(_Controlled_by_Enable_1_), M2.pin_2
  N5: IC1.In_2, Composant1.D4
  N6: IC1.+Vmotor, VCC1.+
  N7: IC1.Enable_2, Composant1.D7
  N8: IC1.In_3, Composant1.D5_PWM
  N9: IC1.Out_3_(_Controlled_by_Enable_2_), M1.pin_1
  N10: IC1.Out_4_(_Controlled_by_Enable_2_), M1.pin_2
  N11: IC1.In_4, Composant1.D6_PWM
  5V: IC1.+V, Composant1.5V, hc-sr1.VCC
  N12: Composant1.D9_PWM, hc-sr1.Echo
  N13: Composant1.D10_PWM/SS, hc-sr1.Trig
